# Fritzing sketch mic_amp (saved by Fritzing 0.9.4)
breadboards: 1

parts:
  Raspberry_Pi_1 = Raspberry Pi 3 [part_number=RPI-3-V1.2]
  IC1 = IC, DIP package, 8 pins [chip_label=IC]
  U1 = MIC [package=mic_electret_smd]
  R1 = Rotary Potentiometer (Small) [maximum_resistance=100kΩ package=THT]

nets:
  N1: Raspberry_Pi_1.GND, IC1.pin4, IC1.pin5, R1.leg2
  N2: Raspberry_Pi_1.5V, IC1.pin1, IC1.pin8
  N3: IC1.pin2, IC1.pin7, U1.2, R1.leg1
  N4: IC1.pin3, IC1.pin6, U1.1
